// Logisim project P3_V1.circ as structural Verilog: 7 circuits, main circuit main
module main (
  input  in_1,
  input  in_2,
  input  [15:0] in_3
);

  wire clock_1_out, controlunit_1_regwrite, controlunit_1_selreadreg1, controlunit_1_selreadreg2;
  wire [1:0] controlunit_1_signalalu;
  wire [2:0] multiplexer_1_out, multiplexer_2_out, rom_1_data_2, rom_1_data_3;
  wire [15:0] adder_1_out, alu_1_result, PC_q, registerfile_1_readdata1, registerfile_1_readdata2,
       registerfile_1_readdata3, registerfile_1_readdata4, rom_1_data;

  Register #(.width(16)) PC (.D(adder_1_out), .en(in_1), .clk(clock_1_out), .Q(PC_q));  // open: clr
  Clock clock_1 (.out(clock_1_out));
  ROM #(.addrWidth(16), .dataWidth(16)) rom_1 (
    .addr(PC_q), .data({rom_1_data[15:11], rom_1_data_3, rom_1_data_2, rom_1_data[4:0]}));
  Adder #(.width(16)) adder_1 (.a(PC_q), .b(in_3), .out(adder_1_out), .cin(in_2));  // open: cout
  Multiplexer #(.width(3)) multiplexer_1 (
    .in0(rom_1_data_3), .in1(rom_1_data_2), .out(multiplexer_1_out), .sel(controlunit_1_selreadreg2));
  Multiplexer #(.width(3)) multiplexer_2 (
    .in0(rom_1_data_2), .in1(rom_1_data[4:2]), .out(multiplexer_2_out), .sel(controlunit_1_selreadreg1));
  ControlUnit controlunit_1 (
    .Opcode(rom_1_data[1:0]), .SelReadReg1(controlunit_1_selreadreg1),
    .SelReadReg2(controlunit_1_selreadreg2), .SignalALU(controlunit_1_signalalu),
    .RegWrite(controlunit_1_regwrite));  // open: in_2
  RegisterFile registerfile_1 (
    .ReadRegister1(multiplexer_2_out), .ReadRegister2(multiplexer_1_out), .RegWrite(controlunit_1_regwrite),
    .WriteRegister(rom_1_data[4:2]), .WriteData(alu_1_result), .Clock(clock_1_out),
    .ReadData1(registerfile_1_readdata1), .ReadData2(registerfile_1_readdata2),
    .ReadData3(registerfile_1_readdata3), .ReadData4(registerfile_1_readdata4));  // open: in_4, in_6
  ALU alu_1 (
    .Immediate({rom_1_data[15:11], rom_1_data_3, rom_1_data_2}), .ArgA(registerfile_1_readdata1),
    .SignalALU(controlunit_1_signalalu), .ArgB(registerfile_1_readdata2), .ArgC(registerfile_1_readdata3),
    .ArgD(registerfile_1_readdata4), .Result(alu_1_result));
endmodule

module RegisterFile (
  input  [2:0] ReadRegister1,
  input  [2:0] ReadRegister2,
  input  RegWrite,
  input  [2:0] in_4,
  input  [2:0] WriteRegister,
  input  [2:0] in_6,
  input  [15:0] WriteData,
  input  Clock,
  output [15:0] ReadData1,
  output [15:0] ReadData2,
  output [15:0] ReadData3,
  output [15:0] ReadData4
);

  wire InR0, InR1, InR2, InR3, InR4, InR5, InR6, InR7;
  wire [2:0] adder_1_out, adder_2_out;
  wire [15:0] OutR0, OutR1, OutR2, OutR3, OutR4, OutR5, OutR6, OutR7;

  Decoder #(.select(3)) decoder_1 (
    .out0(InR0), .out1(InR1), .out2(InR2), .out3(InR3), .out4(InR4), .out5(InR5), .out6(InR6), .out7(InR7),
    .sel(WriteRegister), .en(RegWrite));
  Register #(.width(16)) R0 (.D(WriteData), .en(InR0), .clk(Clock), .Q(OutR0));  // open: clr
  Register #(.width(16)) R1 (.D(WriteData), .en(InR1), .clk(Clock), .Q(OutR1));  // open: clr
  Register #(.width(16)) R2 (.D(WriteData), .en(InR2), .clk(Clock), .Q(OutR2));  // open: clr
  Register #(.width(16)) R3 (.D(WriteData), .en(InR3), .clk(Clock), .Q(OutR3));  // open: clr
  Register #(.width(16)) R4 (.D(WriteData), .en(InR4), .clk(Clock), .Q(OutR4));  // open: clr
  Register #(.width(16)) R5 (.D(WriteData), .en(InR5), .clk(Clock), .Q(OutR5));  // open: clr
  Multiplexer #(.select(3), .width(16)) multiplexer_1 (
    .in0(OutR0), .in1(OutR1), .in2(OutR2), .in3(OutR3), .in4(OutR4), .in5(OutR5), .in6(OutR6), .in7(OutR7),
    .out(ReadData1), .sel(ReadRegister1));
  Adder #(.width(3)) adder_1 (.a(ReadRegister1), .b(in_4), .out(adder_1_out));  // open: cin, cout
  Multiplexer #(.select(3), .width(16)) multiplexer_2 (
    .in0(OutR0), .in1(OutR1), .in2(OutR2), .in3(OutR3), .in4(OutR4), .in5(OutR5), .in6(OutR6), .in7(OutR7),
    .out(ReadData3), .sel(adder_1_out));
  Register #(.width(16)) R6 (.D(WriteData), .en(InR6), .clk(Clock), .Q(OutR6));  // open: clr
  Register #(.width(16)) R7 (.D(WriteData), .en(InR7), .clk(Clock), .Q(OutR7));  // open: clr
  Adder #(.width(3)) adder_2 (.a(ReadRegister2), .b(in_6), .out(adder_2_out));  // open: cin, cout
  Multiplexer #(.select(3), .width(16)) multiplexer_3 (
    .in0(OutR0), .in1(OutR1), .in2(OutR2), .in3(OutR3), .in4(OutR4), .in5(OutR5), .in6(OutR6), .in7(OutR7),
    .out(ReadData2), .sel(ReadRegister2));
  Multiplexer #(.select(3), .width(16)) multiplexer_4 (
    .in0(OutR0), .in1(OutR1), .in2(OutR2), .in3(OutR3), .in4(OutR4), .in5(OutR5), .in6(OutR6), .in7(OutR7),
    .out(ReadData4), .sel(adder_2_out));
endmodule

module ControlUnit (
  input  [1:0] Opcode,
  input  in_2,
  output SelReadReg1,
  output SelReadReg2,
  output [1:0] SignalALU,
  output RegWrite
);

  wire not_1_out;

  not not_1 (not_1_out, Opcode[1]);
  and and_1 (SelReadReg2, Opcode[0], not_1_out);

  assign RegWrite = in_2;
  assign SelReadReg1 = Opcode[0];
  assign SignalALU = Opcode;
endmodule

module ALU (
  input  [10:0] Immediate,
  input  [15:0] ArgA,
  input  [1:0] SignalALU,
  input  [15:0] ArgB,
  input  [15:0] ArgC,
  input  [15:0] ArgD,
  output [15:0] Result
);

  wire [15:0] add_1_result, dot_1_result, Dota_result, li_1_result;

  Li li_1 (.Immediate(Immediate), .Result(li_1_result));
  add add_1 (.ArgA(ArgA), .ArgB(ArgB), .Result(add_1_result));  // open: in_2
  dot dot_1 (.ArgA(ArgA), .ArgB(ArgB), .ArgC(ArgC), .ArgD(ArgD), .Result(dot_1_result));  // open: in_3
  Multiplexer #(.select(2), .width(16)) multiplexer_1 (
    .in0(li_1_result), .in1(add_1_result), .in2(dot_1_result), .in3(Dota_result), .out(Result),
    .sel(SignalALU));
  add Dota (.ArgA(ArgA), .ArgB(dot_1_result), .Result(Dota_result));  // open: in_2
endmodule

module Li (
  input  [10:0] Immediate,
  output [15:0] Result
);

  assign Result = {{5{Immediate[10]}}, Immediate};  // Bit_Extender bit_extender_1
endmodule

module add (
  input  [15:0] ArgA,
  input  in_2,
  input  [15:0] ArgB,
  output [15:0] Result
);

  Adder #(.width(16)) adder_1 (.a(ArgA), .b(ArgB), .out(Result), .cin(in_2));  // open: cout
endmodule

module dot (
  input  [15:0] ArgA,
  input  [15:0] ArgB,
  input  in_3,
  input  [15:0] ArgC,
  input  [15:0] ArgD,
  output [15:0] Result
);

  wire [15:0] multiplier_1_out, multiplier_2_out;

  Multiplier #(.width(16)) multiplier_1 (.a(ArgA), .b(ArgB), .out(multiplier_1_out));  // open: cin, cout
  Multiplier #(.width(16)) multiplier_2 (.a(ArgC), .b(ArgD), .out(multiplier_2_out));  // open: cin, cout
  Adder #(.width(16)) adder_1 (.a(multiplier_1_out), .b(multiplier_2_out), .out(Result), .cin(in_3));  // open: cout
endmodule
